// Logisim project var1.circ as structural Verilog: 4 circuits, main circuit 1
module _1 (
  input  X0,
  input  X1,
  output Y3,
  output Y2,
  output Y1,
  output Y0
);

  wire not_1_out, not_2_out, not_3_out, not_4_out, or_1_out, or_2_out, or_3_out, or_4_out;

  not not_1 (not_1_out, X0);
  not not_2 (not_2_out, X1);
  not not_3 (not_3_out, X0);
  not not_4 (not_4_out, X1);
  or or_1 (or_1_out, not_1_out, not_2_out);
  or or_2 (or_2_out, not_3_out, X1);
  or or_3 (or_3_out, X0, not_4_out);
  or or_4 (or_4_out, X0, X1);
  not not_5 (Y3, or_1_out);
  not not_6 (Y2, or_2_out);
  not not_7 (Y1, or_3_out);
  not not_8 (Y0, or_4_out);
endmodule

module _2 (
  input  X2,
  input  X1,
  input  X0,
  input  X3,
  input  X4,
  output Y0,
  output Y1,
  output Y2,
  output Y3,
  output Y4,
  output Y5,
  output Y6,
  output Y7,
  output Y8,
  output Y9,
  output Y10,
  output Y11,
  output Y12,
  output Y13,
  output Y14,
  output Y15,
  output Y16,
  output Y17,
  output Y18,
  output Y19,
  output Y20,
  output Y21,
  output Y22,
  output Y23
);

  wire decoder_1_out0, decoder_1_out1, decoder_1_out2;

  Decoder #(.select(2)) decoder_1 (
    .out0(decoder_1_out0), .out1(decoder_1_out1), .out2(decoder_1_out2), .sel({X4, X3}), .en(1'b1));  // open: out3
  Decoder #(.select(3), .disabled(0)) decoder_2 (
    .out0(Y0), .out1(Y1), .out2(Y2), .out3(Y3), .out4(Y4), .out5(Y5), .out6(Y6), .out7(Y7),
    .sel({X0, X1, X2}), .en(decoder_1_out0));
  Decoder #(.select(3), .disabled(0)) decoder_3 (
    .out0(Y8), .out1(Y9), .out2(Y10), .out3(Y11), .out4(Y12), .out5(Y13), .out6(Y14), .out7(Y15),
    .sel({X0, X1, X2}), .en(decoder_1_out1));
  Decoder #(.select(3), .disabled(0)) decoder_4 (
    .out0(Y16), .out1(Y17), .out2(Y18), .out3(Y19), .out4(Y20), .out5(Y21), .out6(Y22), .out7(Y23),
    .sel({X0, X1, X2}), .en(decoder_1_out2));
endmodule

module _3 (
  input  X1,
  input  X2,
  input  X3,
  output Y
);

  wire decoder_1_out4, decoder_1_out6, decoder_1_out7;

  Decoder #(.select(3), .enable("false")) decoder_1 (
    .out4(decoder_1_out4), .out6(decoder_1_out6), .out7(decoder_1_out7), .sel({X3, X2, X1}));  // open: out0, out1, out2, out3, out5
  or or_1 (Y, decoder_1_out4, decoder_1_out6, decoder_1_out7);
endmodule

module _4 (
  input  X0,
  input  X1,
  input  X2,
  input  X3,
  output Y0,
  output Y1
);

  or or_1 (Y0, X1, X3);
  or or_2 (Y1, X2, X3);
endmodule
