// Logisim project var1.circ as structural Verilog: 1 circuit, main circuit 1
module _1 (
  input  X0,
  input  X1,
  input  X2,
  input  X3,
  output Y0,
  output Y1,
  output Y2,
  output Y3
);

  wire decoder_1_out1, decoder_1_out2, decoder_1_out3, decoder_1_out4, decoder_1_out5, decoder_1_out6,
       decoder_1_out7, decoder_1_out8, decoder_1_out9, decoder_1_out10, decoder_1_out11, decoder_1_out12,
       decoder_1_out13, decoder_1_out14, decoder_1_out15;

  Decoder #(.select(4)) decoder_1 (
    .out1(decoder_1_out1), .out2(decoder_1_out2), .out3(decoder_1_out3), .out4(decoder_1_out4),
    .out5(decoder_1_out5), .out6(decoder_1_out6), .out7(decoder_1_out7), .out8(decoder_1_out8),
    .out9(decoder_1_out9), .out10(decoder_1_out10), .out11(decoder_1_out11), .out12(decoder_1_out12),
    .out13(decoder_1_out13), .out14(decoder_1_out14), .out15(decoder_1_out15), .sel({X3, X2, X1, X0}),
    .en(1'b1));  // open: out0
  or or_1 (Y0, decoder_1_out1, decoder_1_out3, decoder_1_out5, decoder_1_out8, decoder_1_out10, decoder_1_out12, decoder_1_out13, decoder_1_out14);
  or or_2 (Y1, decoder_1_out2, decoder_1_out3, decoder_1_out6, decoder_1_out9, decoder_1_out10, decoder_1_out14);
  or or_3 (Y2, decoder_1_out4, decoder_1_out5, decoder_1_out6, decoder_1_out11, decoder_1_out12, decoder_1_out13, decoder_1_out14);
  or or_4 (Y3, decoder_1_out7, decoder_1_out8, decoder_1_out9, decoder_1_out10, decoder_1_out11, decoder_1_out12, decoder_1_out13, decoder_1_out14);
endmodule
