// Logisim project var1.circ as structural Verilog: 2 circuits, main circuit 1
module _1 (
  input  A0,
  input  B0,
  input  A1,
  input  B1,
  output Y
);

  wire xnor_1_out, xnor_2_out;

  xnor xnor_1 (xnor_1_out, A0, B0);
  xnor xnor_2 (xnor_2_out, A1, B1);
  and and_1 (Y, xnor_1_out, xnor_2_out);
endmodule

module _2 (
  input  A0,
  input  B0,
  input  A1,
  input  B1,
  input  A2,
  input  B2,
  output out_7,
  output out_8,
  output out_9
);

  wire and_1_out, and_2_out, and_3_out, and_4_out, and_5_p3, and_5_p4, xnor_1_out, xnor_2_out, xnor_3_out;

  xnor xnor_1 (xnor_1_out, A0, B0);
  xnor xnor_2 (xnor_2_out, A1, B1);
  xnor xnor_3 (xnor_3_out, A2, B2);
  and and_1 (and_1_out, ~A0, B0);  // AND_Gate
  and and_2 (and_2_out, B1, ~A1);  // AND_Gate
  and and_3 (and_3_out, B2, ~A2);  // AND_Gate
  // AND_Gate and_4 has open pins: out=and_4_out
  // AND_Gate and_5: pin names not known; wires that end beside it: B1, A1, and_5_p3, and_5_p4
  // AND_Gate and_6: pin names not known; wires that end beside it: A1, and_5_p4
  or or_1 (out_7, and_1_out, and_2_out, and_3_out);
  and and_7 (out_8, xnor_1_out, xnor_3_out);
  or or_2 (out_9, and_4_out, and_5_p3, and_5_p4);
endmodule
